# Fritzing sketch Ultra_RBBB_V01 (saved by Fritzing 0.8.3b)
circuit board: 4.09877cm x 1.55645cm
breadboards: 1

parts:
  U1 = atmega328 [package=dip]
  XTAL1 = Crystal [frequency="16 Mhz" package=THT]
  C1 = Ceramic Capacitor [capacitance=100nF package="100 mil [THT, multilayer]"]
  C2 = Ceramic Capacitor [capacitance=100nF package="100 mil [THT, multilayer]"]
  R1 = Resistor [tolerance=±5% resistance=220 package=THT]
  J2 = female pin header, 14 pins [form="♀ (female)"]
  PWR1 = female pin header, 6 pins [form="♀ (female)"]
  C3 = Ceramic Capacitor [capacitance=100nF package="100 mil [THT, multilayer]"]
  PWR = female pin header, 3 pins [form="♀ (female)"]
  PWR2 = female pin header, 2 pins [form="♀ (female)"]
  J3 = female pin header, 4 pins [form="♀ (female)"]
  J4 = female pin header, 8 pins [form="♀ (female)"]

nets:
  N1: U1.RESET, R1.Pin_1, C3.1, J4.pin1
  N2: U1.D0_(RX), PWR1.pin3, J4.pin2
  N3: U1.D1_(TX), PWR1.pin2, J4.pin3
  N4: U1.D2, J4.pin4
  N5: U1.D3_(PWM), J4.pin5
  N6: U1.D4, J4.pin6
  N7: U1.VCC, U1.AVCC, R1.Pin_0, J2.pin9, PWR1.pin4, PWR2.pin2, J4.pin7
  N8: U1.GND, C1.0, C2.0, J2.pin7, PWR1.pin6, PWR.pin2, J4.pin8
  N9: U1.XLAT1, XTAL1.pin_1, C2.1
  N10: U1.XLAT2, XTAL1.pin_0, C1.1
  N11: U1.D5_(PWM), J3.pin1
  N12: U1.D6_(PWM), J3.pin2
  N13: U1.D7, J3.pin3
  N14: U1.D8, J3.pin4
  N15: U1.D9_(PWM), J2.pin14
  N16: U1.D10_(PWM), J2.pin13
  N17: U1.D11_(PWM), J2.pin12
  N18: U1.D12, J2.pin11
  N19: U1.D13, J2.pin10
  N20: U1.AREF, J2.pin8
  N21: U1.A0, J2.pin6
  N22: U1.A1, J2.pin5
  N23: U1.A2, J2.pin4
  N24: U1.A3, J2.pin3
  N25: U1.A4, J2.pin2
  N26: U1.A5, J2.pin1
  N27: PWR1.pin1, C3.0
  N28: PWR.pin3, PWR2.pin1

notes:
  -
